# Fritzing sketch schema (saved by Fritzing 0.9.2b)

parts:
  GY1 = MPU-6050 Board GY-521 [form="♀ (female)" package=THT]
  Part1 = Arduino Uno (Rev3)
  Part2 = Intel Galileo

nets:
  N1: GY1.pin1, Part1.3V3
  GND: GY1.pin2, Part1.GND, Part2.GND
  N2: GY1.pin3, Part1.A5/SCL
  N3: GY1.pin4, Part1.A4/SDA
  N4: GY1.pin8, Part1.D2
  N5: Part1.D0/RX, Part2.D1/TX
  N6: Part1.D1/TX, Part2.D0/RX
  5V: Part1.5V, Part2.5V

custom parts:
  MPU-6050 Board GY-521: Acelerometro y Giroscopio MPU-6050 Board GY-521
